# Fritzing sketch ThreeSwitches (saved by Fritzing 0.9.10b)
circuit board: 8.44007cm x 5.5114cm
breadboards: 1

parts:
  Part2 = songle relay
  Part3 = songle relay
  Part1 = songle relay
  Part4 = Arduino Nano (Rev3.0)
  Q1 = NPN-Transistor [package="TO92 [THT]"]
  Q2 = NPN-Transistor [package="TO92 [THT]"]
  Q3 = NPN-Transistor [package="TO92 [THT]"]
  J5 = Screw terminal - 2 pins [package=THT]
  D1 = Rectifier Diode [part_number=1N4001 package="300 mil [THT]"]
  D2 = Rectifier Diode [part_number=1N4001 package="300 mil [THT]"]
  D3 = Rectifier Diode [part_number=1N4001 package="300 mil [THT]"]
  R1 = Resistor [tolerance=±5% power=0.25 resistance=1k package=THT]
  R2 = Resistor [tolerance=±5% power=0.25 resistance=1k package=THT]
  R3 = Resistor [tolerance=±5% power=0.25 resistance=1k package=THT]
  J10 = JST-03JQ-BT [part_number=JST-JQ-BT package=THT]
  J11 = JST-03JQ-BT [part_number=JST-JQ-BT package=THT]
  J12 = JST-03JQ-BT [part_number=JST-JQ-BT package=THT]
  R4 = Resistor [tolerance=±5% power=0.25 resistance=1k package=THT]
  R5 = Resistor [tolerance=±5% power=0.25 resistance=1k package=THT]
  R6 = Resistor [tolerance=±5% power=0.25 resistance=1k package=THT]
  J13 = screw terminal, 3 pins
  J14 = JST-03JQ-BT [part_number=JST-JQ-BT package=THT]
  J15 = JST-03JQ-BT [part_number=JST-JQ-BT package=THT]
  J16 = JST-03JQ-BT [part_number=JST-JQ-BT package=THT]

nets:
  N1: Part2.VCC, Q3.C, D2.anode
  N2: Part2.NO, J11.pin1
  N3: Part2.NC, J11.pin3
  N4: Part2.COMMON, J11.pin2
  GND: Part2.GND, Part3.GND, Part1.GND, Part4.VIN, J5.pin2, D1.cathode, D2.cathode, J14.pin2, J15.pin2, J16.pin2
  N5: Part3.VCC, Q1.C, D3.anode
  N6: Part3.NO, J12.pin1
  N7: Part3.NC, J12.pin3
  N8: Part3.COMMON, J12.pin2
  N9: Part1.VCC, Q2.C, D1.anode
  N10: Part1.NO, J10.pin1
  N11: Part1.NC, J10.pin3
  N12: Part1.COMMON, J10.pin2
  N13: Part4.GND, Q1.E, Q2.E, Q3.E, J5.pin1, R4.Pin_1, R5.Pin_1, R6.Pin_1, J14.pin1, J15.pin1, J16.pin1
  N14: Part4.D2, J14.pin3
  N15: Part4.D3, R2.Pin_1
  N16: Part4.D4, R4.Pin_0, J13.pin1
  N17: Part4.D5, J15.pin3
  N18: Part4.D6, R1.Pin_1
  N19: Part4.D7, R5.Pin_0, J13.pin2
  N20: Part4.D8, J16.pin3
  N21: Part4.D9, R3.Pin_1
  N22: Part4.D10, R6.Pin_0, J13.pin3
  N23: Q1.B, R3.Pin_0
  N24: Q2.B, R2.Pin_0
  N25: Q3.B, R1.Pin_0
